# Fritzing sketch MQ2 (saved by Fritzing 0.9.2b)
breadboards: 1

parts:
  R2 = Resistor [tolerance=±5% resistance=220 package=THT]
  R1 = Resistor [tolerance=±5% resistance=330 package=THT]
  U1 = ESP32-38PinWide [part_number=ESP32-38PinWide]
  module1 = MQ-2 Gas Sensor

nets:
  N1: R2.Pin_1, R1.Pin_0, U1.GPIO34
  GND: R1.Pin_1, U1.GND, module1.AO, module1.GND
  VIN: U1.VIN, module1.VCC

custom parts:
  ESP32-38PinWide: Generic 38-Pin ESP32 with wide format (only access to one side of pins on a breadboard) based on Stephen Lilley's HiLetgo ESP-WROOM-32 ESP32 ESP-32S Development Board.
  MQ-2 Gas Sensor: MQ-2 Gas Sensor module of SunFounder Sensor Kit
